// Digital circuit alu_wired.dig as structural Verilog
module alu_wired (
  input  [7:0] DATA,
  input  A_LD,
  input  A_OE,
  input  A_SEL,
  input  ALU_S0,
  input  ALU_S1,
  input  ALU_S2,
  input  ALU_OE,
  input  ALU_CIN,
  input  SHR,
  input  RST,
  input  CLK,
  input  ROR,
  output [7:0] DATA_2,
  output C_FLAG,
  output V_FLAG,
  output N_FLAG,
  output Z_FLAG
);

  wire A_LD_t, A_OE_t, AA0, AA1, AA2, AA3, AA4, AA5, AA6, AA7, AL0, AL1, AL2, AL3, AL4, AL5, AL6, ALCO,
       ALU_OE_t, AO0, AO1, AO2, AO3, AO4, AO5, AO6, AO7, O0, O1, O2, O3, ROR_t, SHR_t;

  not not_1 (A_LD_t, A_LD);
  not not_2 (A_OE_t, A_OE);
  not not_3 (ALU_OE_t, ALU_OE);
  not not_4 (SHR_t, SHR);
  not not_5 (ROR_t, ROR);
  _74245 _74245_1 (
    .pin1(1'b0), .pin2(DATA[0]), .pin3(DATA[1]), .pin4(DATA[2]), .pin5(DATA[3]), .pin6(DATA[4]),
    .pin7(DATA[5]), .pin8(DATA[6]), .pin9(DATA[7]), .pin10(1'b0), .pin11(AO7), .pin12(AO6), .pin13(AO5),
    .pin14(AO4), .pin15(AO3), .pin16(AO2), .pin17(AO1), .pin18(AO0), .pin19(A_OE_t), .pin20(1'b1));
  _74245 _74245_2 (
    .pin1(1'b0), .pin2(DATA[0]), .pin3(DATA[1]), .pin4(DATA[2]), .pin5(DATA[3]), .pin6(DATA[4]),
    .pin7(DATA[5]), .pin8(DATA[6]), .pin9(DATA[7]), .pin10(1'b0), .pin11(1'b0), .pin12(AO7), .pin13(AO6),
    .pin14(AO5), .pin15(AO4), .pin16(AO3), .pin17(AO2), .pin18(AO1), .pin19(SHR_t), .pin20(1'b1));
  _74245 _74245_3 (
    .pin1(1'b0), .pin2(DATA[0]), .pin3(DATA[1]), .pin4(DATA[2]), .pin5(DATA[3]), .pin6(DATA[4]),
    .pin7(DATA[5]), .pin8(DATA[6]), .pin9(DATA[7]), .pin10(1'b0), .pin11(AO7), .pin12(AO6), .pin13(AO5),
    .pin14(AO4), .pin15(AO3), .pin16(AO2), .pin17(AO1), .pin18(C_FLAG), .pin19(ROR_t), .pin20(1'b1));
  _74257 _74257_1 (
    .pin1(A_SEL), .pin2(DATA[0]), .pin3(AL0), .pin4(AA0), .pin5(DATA[1]), .pin6(AL1), .pin7(AA1),
    .pin8(1'b0), .pin9(AA2), .pin10(AL2), .pin11(DATA[2]), .pin12(AA3), .pin13(AL3), .pin14(DATA[3]),
    .pin15(1'b0), .pin16(1'b1));
  _74173 _74173_1 (
    .pin1(1'b0), .pin2(1'b0), .pin3(AO0), .pin4(AO1), .pin5(AO2), .pin6(AO3), .pin7(CLK), .pin8(1'b0),
    .pin9(A_LD_t), .pin10(A_LD_t), .pin11(AA3), .pin12(AA2), .pin13(AA1), .pin14(AA0), .pin15(RST),
    .pin16(1'b1));
  _74382 _74382_1 (
    .pin1(AO1), .pin2(DATA[1]), .pin3(AO0), .pin4(DATA[0]), .pin5(ALU_S0), .pin6(ALU_S1), .pin7(ALU_S2),
    .pin8(AL0), .pin9(AL1), .pin10(1'b0), .pin11(AL2), .pin12(AL3), .pin14(ALCO), .pin15(ALU_CIN),
    .pin16(DATA[3]), .pin17(AO3), .pin18(DATA[2]), .pin19(AO2), .pin20(1'b1));  // open: pin13
  _74245 _74245_4 (
    .pin1(1'b0), .pin2(DATA_2[0]), .pin3(DATA_2[1]), .pin4(DATA_2[2]), .pin5(DATA_2[3]), .pin6(DATA_2[4]),
    .pin7(DATA_2[5]), .pin8(DATA_2[6]), .pin9(DATA_2[7]), .pin10(1'b0), .pin11(N_FLAG), .pin12(AL6),
    .pin13(AL5), .pin14(AL4), .pin15(AL3), .pin16(AL2), .pin17(AL1), .pin18(AL0), .pin19(ALU_OE_t),
    .pin20(1'b1));
  _74257 _74257_2 (
    .pin1(A_SEL), .pin2(DATA[4]), .pin3(AL4), .pin4(AA4), .pin5(DATA[5]), .pin6(AL5), .pin7(AA5),
    .pin8(1'b0), .pin9(AA6), .pin10(AL6), .pin11(DATA[6]), .pin12(AA7), .pin13(N_FLAG), .pin14(DATA[7]),
    .pin15(1'b0), .pin16(1'b1));
  _74173 _74173_2 (
    .pin1(1'b0), .pin2(1'b0), .pin3(AO4), .pin4(AO5), .pin5(AO6), .pin6(AO7), .pin7(CLK), .pin8(1'b0),
    .pin9(A_LD_t), .pin10(A_LD_t), .pin11(AA7), .pin12(AA6), .pin13(AA5), .pin14(AA4), .pin15(RST),
    .pin16(1'b1));
  _74382 _74382_2 (
    .pin1(AO5), .pin2(DATA[5]), .pin3(AO4), .pin4(DATA[4]), .pin5(ALU_S0), .pin6(ALU_S1), .pin7(ALU_S2),
    .pin8(AL4), .pin9(AL5), .pin10(1'b0), .pin11(AL6), .pin12(N_FLAG), .pin13(V_FLAG), .pin14(C_FLAG),
    .pin15(ALCO), .pin16(DATA[7]), .pin17(AO7), .pin18(DATA[6]), .pin19(AO6), .pin20(1'b1));
  _7421 _7421_1 (
    .pin1(O0), .pin2(O1), .pin4(O2), .pin5(O3), .pin6(Z_FLAG), .pin7(1'b0), .pin9(1'b0), .pin10(1'b0),
    .pin12(1'b0), .pin13(1'b0), .pin14(1'b1));  // open: pin3, pin8, pin11
  _7402 _7402_1 (
    .pin1(O0), .pin2(AL0), .pin3(AL1), .pin4(O1), .pin5(AL2), .pin6(AL3), .pin7(1'b0), .pin8(AL4),
    .pin9(AL5), .pin10(O2), .pin11(AL6), .pin12(N_FLAG), .pin13(O3), .pin14(1'b1));

  // Other names for the same wires on the sheet: AL7 = N_FLAG; ALC = C_FLAG; ALV = V_FLAG; ALZ = Z_FLAG; D0 = DATA[0];
  //   D1 = DATA[1]; D2 = DATA[2]; D3 = DATA[3]; D4 = DATA[4]; D5 = DATA[5]; D6 = DATA[6]; D7 = DATA[7];
  //   DO0 = DATA_2[0]; DO1 = DATA_2[1]; DO2 = DATA_2[2]; DO3 = DATA_2[3]; DO4 = DATA_2[4]; DO5 = DATA_2[5];
  //   DO6 = DATA_2[6]; DO7 = DATA_2[7]
endmodule
