// Digital circuit ADDRESSDECODER.dig as structural Verilog
module ADDRESSDECODER (
  input  [15:0] A_BUS,
  output nRAM_CS,
  output nROM_CS,
  output nFB_CS,
  output nMMIO_CS
);

  wire _7400_1_pin3, _74139_1_pin7, _74139_1_pin15;

  _74139 _74139_1 (
    .pin1(1'b0), .pin2(A_BUS[14]), .pin3(A_BUS[15]), .pin7(_74139_1_pin7), .pin8(1'b0), .pin9(nMMIO_CS),
    .pin13(A_BUS[9]), .pin14(A_BUS[8]), .pin15(_74139_1_pin15), .pin16(1'b1));  // open: pin4, pin5, pin6, pin10, pin11, pin12
  _74138 _74138_1 (
    .pin1(A_BUS[11]), .pin2(A_BUS[12]), .pin3(A_BUS[13]), .pin4(1'b0), .pin5(1'b0), .pin6(A_BUS[10]),
    .pin7(_74139_1_pin15), .pin8(1'b0), .pin16(1'b1));  // open: pin9, pin10, pin11, pin12, pin13, pin14, pin15
  _7400 _7400_1 (
    .pin1(_74139_1_pin15), .pin2(_74139_1_pin15), .pin3(_7400_1_pin3), .pin4(_74139_1_pin7),
    .pin5(_74139_1_pin7), .pin6(nRAM_CS), .pin7(1'b0), .pin8(nROM_CS), .pin9(nRAM_CS),
    .pin10(_74139_1_pin15), .pin11(nFB_CS), .pin12(nMMIO_CS), .pin13(_7400_1_pin3), .pin14(1'b1));
endmodule
