// Digital circuit ADDR_DEC.dig as structural Verilog
module ADDR_DEC (
  input  [15:0] A_IN,
  output nRAM_CS,
  output nROM_CS,
  output nMMIO_CS
);

  wire _7430_1_pin1;

  _7430 _7430_1 (
    .pin1(_7430_1_pin1), .pin2(A_IN[8]), .pin3(A_IN[9]), .pin4(A_IN[12]), .pin5(A_IN[13]), .pin6(A_IN[15]),
    .pin7(1'b0), .pin8(nMMIO_CS), .pin11(A_IN[11]), .pin12(A_IN[10]), .pin14(1'b1));  // open: pin9, pin10, pin13
  _7400 _7400_1 (
    .pin1(A_IN[14]), .pin2(A_IN[15]), .pin3(nROM_CS), .pin4(A_IN[14]), .pin5(A_IN[14]), .pin6(_7430_1_pin1),
    .pin7(1'b0), .pin9(1'b0), .pin10(1'b0), .pin11(nRAM_CS), .pin12(nROM_CS), .pin13(nMMIO_CS), .pin14(1'b1));  // open: pin8
endmodule
