// Digital circuit ADR_DEC.dig as structural Verilog
module ADR_DEC (
  input  [15:0] A_IN,
  output nRAM_CS,
  output nROM_CS,
  output nFB_CS,
  output nMMIO_CS
);

  wire _7408_1_pin4, _7408_1_pin5, _7408_1_pin9, _7408_1_pin10, _7408_1_pin12, _7408_1_pin13, _74138_1_pin7;

  _74138 _74138_1 (
    .pin1(A_IN[11]), .pin2(A_IN[12]), .pin3(A_IN[13]), .pin4(1'b0), .pin5(1'b0), .pin6(nRAM_CS),
    .pin7(_74138_1_pin7), .pin8(1'b0), .pin12(_74138_1_pin7), .pin16(1'b1));  // open: pin9, pin10, pin11, pin13, pin14, pin15
  _7408 _7408_1 (
    .pin1(A_IN[14]), .pin2(A_IN[15]), .pin3(nRAM_CS), .pin4(_7408_1_pin4), .pin5(_7408_1_pin5),
    .pin6(nFB_CS), .pin7(1'b0), .pin8(_7408_1_pin4), .pin9(_7408_1_pin9), .pin10(_7408_1_pin10),
    .pin11(_7408_1_pin5), .pin12(_7408_1_pin12), .pin13(_7408_1_pin13), .pin14(1'b1));
  _74138 _74138_2 (
    .pin1(A_IN[8]), .pin2(A_IN[9]), .pin3(A_IN[10]), .pin4(_74138_1_pin7), .pin5(1'b0), .pin6(1'b1),
    .pin7(nMMIO_CS), .pin8(1'b0), .pin9(_7408_1_pin13), .pin10(_7408_1_pin12), .pin11(_7408_1_pin10),
    .pin12(_7408_1_pin9), .pin16(1'b1));  // open: pin13, pin14, pin15
  _7410 _7410_1 (
    .pin1(1'b0), .pin2(1'b0), .pin3(nMMIO_CS), .pin4(nFB_CS), .pin5(nRAM_CS), .pin6(nROM_CS), .pin7(1'b0),
    .pin9(1'b0), .pin10(1'b0), .pin11(1'b0), .pin13(1'b0), .pin14(1'b1));  // open: pin8, pin12
endmodule
