// Digital circuit CPU.dig as structural Verilog
module CPU (
  input  RST,
  input  CLK,
  input  clk_2,
  input  CLK_SEL,
  input  nSTOP,
  output [7:0] opcode,
  output [15:0] rom,
  output [3:0] step
);

  wire A_LD, A_OE, A_SEL, addr_dec_1_nram_cs, addr_dec_1_nrom_cs, alu_1_c_flag, alu_1_n_flag, alu_1_v_flag,
       alu_1_z_flag, ALU_CIN, ALU_S0, ALU_S1, ALU_S2, and_1_out, and_2_out, B_SET, C, CLK_t, FL_SEL, I,
       I_SET, I_WRITE, interrupts_1_p11, K_av, MAR_DIR, MEM_RD, MEM_WR, mmio_1_kb_en, N, nALU_OE, nFL_LD,
       nFL_OE, nHBA_OE, nIR_LD, nIRA_OE, nIRD_OE, nIRQ_CLR, nMAR_INC, nMAR_OE, nMARH_LD, nMARL_LD, nMMIO_CS,
       nMPC_RST, not_2_out, not_3_out, not_4_out, nPC_LD, nPCH_OE, nPCL_OE, nRST, nSHR, nSP_INC, nSP_LD,
       nSP_OE, nSPH_OE, nSPL_OE, nV_OE, nXY_AOE, nXY_INC, PC_INC, PC_OE, REG_LD, REG_OE, SHR_IN0, SP_DIR, V,
       V_B0, XY_DIR, Z;
  wire [2:0] Rsrc;
  wire [3:0] mmio_1_spi_out;
  wire [7:0] alu_1_alu, keyboard_1_d, mmio_1_display, pc_1_d_out, rst_buffer_1_p2, rst_buffer_1_p3;
  wire [15:8] keyboard_1_d_2;
  wire [15:13] ctrlunit_1_c32_47;

  not not_1 (nRST, RST);
  and and_1 (and_1_out, CLK, ~CLK_SEL);  // And
  and and_2 (and_2_out, CLK_SEL, clk_2);
  or or_1 (CLK_t, and_1_out, and_2_out);
  not not_2 (not_2_out, RST);
  // A_H__BUFFER a_h__buffer_1: pin names not known; wires that end beside it: nHBA_OE
  // RST_Buffer rst_buffer_1: pin names not known; wires that end beside it: not_2_out, rst_buffer_1_p2, {rst_buffer_1_p2, rst_buffer_1_p3}
  ADDR_DEC addr_dec_1 (
    .A_IN({rst_buffer_1_p2, rst_buffer_1_p3}), .nRAM_CS(addr_dec_1_nram_cs), .nROM_CS(addr_dec_1_nrom_cs),
    .nMMIO_CS(nMMIO_CS));
  PC pc_1 (
    .A_IN({rst_buffer_1_p2, rst_buffer_1_p3}), .PC_INC(PC_INC), .nPC_LD(nPC_LD), .PC_OE(PC_OE),
    .nPCL_OE(nPCL_OE), .nPCH_OE(nPCH_OE), .CLK(CLK_t), .RST(RST), .A_OUT({rst_buffer_1_p2, rst_buffer_1_p3}),
    .D_OUT(pc_1_d_out));
  SP sp_1 (
    .A_IN({rst_buffer_1_p2, rst_buffer_1_p3}), .nSP_INC(nSP_INC), .SP_DIR(SP_DIR), .nSP_LD(nSP_LD),
    .nSP_OE(nSP_OE), .nSPH_OE(nSPH_OE), .nSPL_OE(nSPL_OE), .CLK(CLK_t),
    .A_OUT({rst_buffer_1_p2, rst_buffer_1_p3}), .D_OUT(pc_1_d_out));
  not not_3 (not_3_out, nSTOP);
  not not_4 (not_4_out, K_av);
  // MAR mar_1: pin names not known; wires that end beside it: {rst_buffer_1_p2, rst_buffer_1_p3}, CLK_t, MAR_DIR, nMAR_INC, nMAR_OE, nMARH_LD, nMARL_LD, pc_1_d_out
  // INTERRUPTS interrupts_1: pin names not known; wires that end beside it: not_3_out, 1'b1, not_4_out, I, nMPC_RST, nV_OE, V_B0, nIRQ_CLR, CLK_t, {rst_buffer_1_p2, rst_buffer_1_p3}, interrupts_1_p11
  RAMSinglePortSel #(.AddrBits(16), .Bits(8)) ramsingleportsel_1 (
    .A({rst_buffer_1_p2, rst_buffer_1_p3}), .CS(~addr_dec_1_nram_cs), .WE(MEM_WR), .OE(MEM_RD), .D(pc_1_d_out));
  EEPROM #(.AddrBits(15), .Bits(16)) eeprom_1 (
    .A({1'b0, rst_buffer_1_p2[5:0], rst_buffer_1_p3}), .CS(~addr_dec_1_nrom_cs), .WE(1'b0), .OE(MEM_RD),
    .D(rom));
  // RFILE rfile_1: pin names not known; wires that end beside it: pc_1_d_out, opcode[2:0], Rsrc, REG_LD, REG_OE, nXY_INC, XY_DIR, nXY_AOE, CLK_t, RST, pc_1_d_out, {rst_buffer_1_p2, rst_buffer_1_p3}, A_LD, A_OE
  ALU alu_1 (
    .D_IN(pc_1_d_out), .A_LD(A_LD), .A_OE(A_OE), .A_SEL(A_SEL), .ALU_S0(ALU_S0), .ALU_S1(ALU_S1),
    .ALU_S2(ALU_S2), .nALU_OE(nALU_OE), .ALU_CIN(ALU_CIN), .nSHR(nSHR), .SHR_IN0(SHR_IN0), .CLK(CLK_t),
    .RST(RST), .ALU(alu_1_alu), .Z_FLAG(alu_1_z_flag), .C_FLAG(alu_1_c_flag), .N_FLAG(alu_1_n_flag),
    .V_FLAG(alu_1_v_flag), .A_R_OUT(pc_1_d_out));
  IR ir_1 (
    .ROM_IN(rom), .nIR_LD(nIR_LD), .nIRD_OE(nIRD_OE), .nIRA_OE(nIRA_OE), .CLK(CLK_t), ._15_11(opcode[7:3]),
    ._10_8(opcode[2:0]), ._7_5(Rsrc), ._0_7(pc_1_d_out), .AB(rst_buffer_1_p3));
  // microPC micropc_1: pin names not known; wires that end beside it: CLK_t, nMPC_RST, step
  MMIO mmio_1 (
    .A_IN({rst_buffer_1_p2, rst_buffer_1_p3}), .D_IN(pc_1_d_out), .nMMIO_CS(nMMIO_CS), .MEM_WR(MEM_WR),
    .MEM_RD(MEM_RD), .KB_IN(keyboard_1_d), .D_OUT(pc_1_d_out), .SPI_OUT(mmio_1_spi_out),
    .DISPLAY(mmio_1_display), .KB_EN(mmio_1_kb_en));  // open: KB_ST
  FLAG_REG flag_reg_1 (
    .D_IN(alu_1_alu), .Z_FLAG(alu_1_z_flag), .C_FLAG(alu_1_c_flag), .N_FLAG(alu_1_n_flag),
    .V_FLAG(alu_1_v_flag), .I_SET(I_SET), .I_WRITE(I_WRITE), .nFL_OE(B_SET), .nFL_LD(nFL_OE),
    .FL_SEL(nFL_LD), .FB(FL_SEL), .CLK(CLK_t), .nRST(nRST), .D_OUT(pc_1_d_out), .Z(Z), .C(C), .N(N), .V(V),
    .I(I));
  CTRLUNIT ctrlunit_1 (
    .OPC(opcode), .microstep(step), .Z(Z), .C(C), .N(N), .V(V), .IRQ(interrupts_1_p11),
    .C0_15({nMAR_INC, nMAR_OE, nMARH_LD, nMARL_LD, MEM_WR, MEM_RD, nMPC_RST, nHBA_OE, nIRA_OE, nIRD_OE, nIR_LD, nPCH_OE, nPCL_OE, PC_OE, nPC_LD, PC_INC}),
    .C16_31({nFL_LD, nFL_OE, SHR_IN0, nSHR, ALU_CIN, nALU_OE, ALU_S2, ALU_S1, ALU_S0, A_SEL, nXY_AOE, XY_DIR, nXY_INC, REG_OE, REG_LD, MAR_DIR}),
    .C32_47({ctrlunit_1_c32_47, V_B0, nV_OE, nIRQ_CLR, nSPH_OE, nSPL_OE, nSP_OE, nSP_LD, SP_DIR, nSP_INC, I_WRITE, I_SET, B_SET, FL_SEL}));
  Keyboard keyboard_1 (.C(mmio_1_kb_en), .en(1'b1), .D({keyboard_1_d_2, keyboard_1_d}), .av(K_av));
  LED SCLK (.in(mmio_1_spi_out[0]));
  LED SDIN (.in(mmio_1_spi_out[1]));
  LED DC (.in(mmio_1_spi_out[2]));
  LED CS (.in(mmio_1_spi_out[3]));
  LED led_1 (.in(mmio_1_display[0]));
  LED led_2 (.in(mmio_1_display[1]));
  LED led_3 (.in(mmio_1_display[2]));
  LED led_4 (.in(mmio_1_display[3]));
  LED led_5 (.in(mmio_1_display[4]));
  LED led_6 (.in(mmio_1_display[5]));
  LED led_7 (.in(mmio_1_display[6]));
  LED led_8 (.in(mmio_1_display[7]));

  // Other names for the same wires on the sheet: Rdst[2:0] = opcode[2:0]

  // Notes on the sheet:
  //   clk_2: Hz: 10
  //   contents of eeprom_1 (hex, n*v repeats v):
  //   fc00,5,dac0,da09,a800,d006,dac0,da0a,ff00,ff00,10aa,11bb,dbc0
  //   ,db0f,ff00,ff00
endmodule
