// Digital circuit CTRLUNIT.dig as structural Verilog
module CTRLUNIT (
  input  [7:0] OPC,
  input  [2:0] microstep,
  input  Z,
  input  C,
  input  N,
  input  V,
  input  I,
  output [15:0] C0_15,
  output [15:0] C16_31,
  output [15:0] C32_47
);

  ROM #(.AddrBits(16), .Bits(16)) _1ROM (.A({I, V, N, C, Z, microstep, OPC}), .sel(1'b1), .D(C0_15));
  ROM #(.AddrBits(16), .Bits(16)) _2ROM (.A({I, V, N, C, Z, microstep, OPC}), .sel(1'b1), .D(C16_31));
  ROM #(.AddrBits(16), .Bits(16)) _3ROM (.A({I, V, N, C, Z, microstep, OPC}), .sel(1'b1), .D(C32_47));

  // Notes on the sheet:
  //   contents of _1ROM (hex, n*v repeats v):
  //   256*f7da,8*f1bb,8*f1fb,e1bb,d1bb,6*f3fb,e1fb,e1fb,6*f3fb,8*f47f
  //   ,8*b5ff,8*f5ff,8*f87f,8*b9ff,16*f9ff,8*f3ff,8*f1fb,8*f1bb,32*f1fb
  //   ,8*f1bb,16*f1fb,16*f1bb,24*f1fb,8*f1bb,b1fd,f1fb,5*f3fb,b1fd,7*f3fb
  //   ,f1fd,f1fb,f1fb,71fb,71fb,fbef,fbef,f1fd,b1fd,b1ff,e3fb,f1ff,f1fb,f1fb
  //   ,f3fb,f1fb,f1fb,fbef,f3ff,f3ff,f1fb,f1fb,f9ff,f3ff,f3fb,88*f3fa
  //   ,8*f5fe,140*f3fa,fbf6,fbf6,f3fa,f3fa,f3fa,d1fa,6*f3fa,fbf6,e7fe
  //   ,f7fe,f3fa,f3fa,f3fa,f5fe,237*f3fa,f1fc,b1fc,10*f3fa,f3ff,d7fe
  //   ,e7fe,253*f3fa,f7de,b1fc,d7fe,253*f3fa,e3ba,f3fa,b1fc,253*f3fa
  //   ,f7de,255*f3fa,d1ba,7*f3fa,256*f7da,8*f1bb,8*f1fb,e1bb,d1bb,6*f3fb
  //   ,e1fb,e1fb,6*f3fb,8*f47f,8*b5ff,8*f5ff,8*f87f,8*b9ff,16*f9ff,8*f3ff
  //   ,8*f1fb,8*f1bb,32*f1fb,8*f1bb,16*f1fb,16*f1bb,24*f1fb,8*f1bb,b1fd
  //   ,f1fb,5*f3fb,b1fd,7*f3fb,f1fd,f1fb,f1fb,71fb,71fb,fbef,fbef,f1fd
  //   ,b1fd,b1ff,e3fb,f1ff,f1fb,f1fb,f3fb,f1fb,f1fb,fbef,f3ff,f3ff,f1fb,f1fb
  //   ,f9ff,f3ff,f3fb,88*f3fa,8*f5fe,140*f3fa,fbf6,fbf6,f3fa,f3fa,f3fa
  //   ,d1fa,6*f3fa,fbf6,e7fe,f7fe,f3fa,f3fa,f3fa,f5fe,237*f3fa,f1fc
  //   ,b1fc,10*f3fa,f3ff,d7fe,e7fe,253*f3fa,f7de,b1fc,d7fe,253*f3fa
  //   ,e3ba,f3fa,b1fc,253*f3fa,f7de,255*f3fa,d1ba,7*f3fa,256*f7da,8*f1bb
  //   ,8*f1fb,e1bb,d1bb,6*f3fb,e1fb,e1fb,6*f3fb,8*f47f,8*b5ff,8*f5ff
  //   ,8*f87f,8*b9ff,16*f9ff,8*f3ff,8*f1fb,8*f1bb,32*f1fb,8*f1bb,16*f1fb
  //   ,16*f1bb,24*f1fb,8*f1bb,b1fd,f1fb,5*f3fb,b1fd,7*f3fb,f1fd,f1fb,f1fb
  //   ,71fb,71fb,fbef,fbef,f1fd,b1fd,b1ff,e3fb,f1ff,f1fb,f1fb,f3fb,f1fb,f1fb
  //   ,fbef,f3ff,f3ff,f1fb,f1fb,f9ff,f3ff,f3fb,88*f3fa,8*f5fe,140*f3fa
  //   ,fbf6,fbf6,f3fa,f3fa,f3fa,d1fa,6*f3fa,fbf6,e7fe,f7fe,f3fa,f3fa,f3fa
  //   ,f5fe,237*f3fa,f1fc,b1fc,10*f3fa,f3ff,d7fe,e7fe,253*f3fa,f7de
  //   ,b1fc,d7fe,253*f3fa,e3ba,f3fa,b1fc,253*f3fa,f7de,255*f3fa,d1ba
  //   ,7*f3fa,256*f7da,8*f1bb,8*f1fb,e1bb,d1bb,6*f3fb,e1fb,e1fb,6*f3fb
  //   ,8*f47f,8*b5ff,8*f5ff,8*f87f,8*b9ff,16*f9ff,8*f3ff,8*f1fb,8*f1bb
  //   ,32*f1fb,8*f1bb,16*f1fb,16*f1bb,24*f1fb,8*f1bb,b1fd,f1fb,5*f3fb
  //   ,b1fd,7*f3fb,f1fd,f1fb,f1fb,71fb,71fb,fbef,fbef,f1fd,b1fd,b1ff
  //   ,e3fb,f1ff,f1fb,f1fb,f3fb,f1fb,f1fb,fbef,f3ff,f3ff,f1fb,f1fb,f9ff
  //   ,f3ff,f3fb,88*f3fa,8*f5fe,140*f3fa,fbf6,fbf6,f3fa,f3fa,f3fa,d1fa
  //   ,6*f3fa,fbf6,e7fe,f7fe,f3fa,f3fa,f3fa,f5fe,237*f3fa,f1fc,b1fc
  //   ,10*f3fa,f3ff,d7fe,e7fe,253*f3fa,f7de,b1fc,d7fe,253*f3fa,e3ba
  //   ,f3fa,b1fc,253*f3fa,f7de,255*f3fa,d1ba,7*f3fa,256*f7da,8*f1bb
  //   ,8*f1fb,e1bb,d1bb,6*f3fb,e1fb,e1fb,6*f3fb,8*f47f,8*b5ff,8*f5ff
  //   ,8*f87f,8*b9ff,16*f9ff,8*f3ff,8*f1fb,8*f1bb,32*f1fb,8*f1bb,16*f1fb
  //   ,16*f1bb,24*f1fb,8*f1bb,b1fd,f1fb,5*f3fb,b1fd,7*f3fb,f1fd,f1fb,f1fb
  //   ,71fb,71fb,fbef,fbef,f1fd,b1fd,b1ff,e3fb,f1ff,f1fb,f1fb,f3fb,f1fb,f1fb
  //   ,fbef,f3ff,f3ff,f1fb,f1fb,f9ff,f3ff,f3fb,88*f3fa,8*f5fe,140*f3fa
  //   ,fbf6,fbf6,f3fa,f3fa,f3fa,d1fa,6*f3fa,fbf6,e7fe,f7fe,f3fa,f3fa,f3fa
  //   ,f5fe,237*f3fa,f1fc,b1fc,10*f3fa,f3ff,d7fe,e7fe,253*f3fa,f7de
  //   ,b1fc,d7fe,253*f3fa,e3ba,f3fa,b1fc,253*f3fa,f7de,255*f3fa,d1ba
  //   ,7*f3fa,256*f7da,8*f1bb,8*f1fb,e1bb,d1bb,6*f3fb,e1fb,e1fb,6*f3fb
  //   ,8*f47f,8*b5ff,8*f5ff,8*f87f,8*b9ff,16*f9ff,8*f3ff,8*f1fb,8*f1bb
  //   ,32*f1fb,8*f1bb,16*f1fb,16*f1bb,24*f1fb,8*f1bb,b1fd,f1fb,5*f3fb
  //   ,b1fd,7*f3fb,f1fd,f1fb,f1fb,71fb,71fb,fbef,fbef,f1fd,b1fd,b1ff
  //   ,e3fb,f1ff,f1fb,f1fb,f3fb,f1fb,f1fb,fbef,f3ff,f3ff,f1fb,f1fb,f9ff
  //   ,f3ff,f3fb,88*f3fa,8*f5fe,140*f3fa,fbf6,fbf6,f3fa,f3fa,f3fa,d1fa
  //   ,6*f3fa,fbf6,e7fe,f7fe,f3fa,f3fa,f3fa,f5fe,237*f3fa,f1fc,b1fc
  //   ,10*f3fa,f3ff,d7fe,e7fe,253*f3fa,f7de,b1fc,d7fe,253*f3fa,e3ba
  //   ,f3fa,b1fc,253*f3fa,f7de,255*f3fa,d1ba,7*f3fa,256*f7da,8*f1bb
  //   ,8*f1fb,e1bb,d1bb,6*f3fb,e1fb,e1fb,6*f3fb,8*f47f,8*b5ff,8*f5ff
  //   ,8*f87f,8*b9ff,16*f9ff,8*f3ff,8*f1fb,8*f1bb,32*f1fb,8*f1bb,16*f1fb
  //   ,16*f1bb,24*f1fb,8*f1bb,b1fd,f1fb,5*f3fb,b1fd,7*f3fb,f1fd,f1fb,f1fb
  //   ,71fb,71fb,fbef,fbef,f1fd,b1fd,b1ff,e3fb,f1ff,f1fb,f1fb,f3fb,f1fb,f1fb
  //   ,fbef,f3ff,f3ff,f1fb,f1fb,f9ff,f3ff,f3fb,88*f3fa,8*f5fe,140*f3fa
  //   ,fbf6,fbf6,f3fa,f3fa,f3fa,d1fa,6*f3fa,fbf6,e7fe,f7fe,f3fa,f3fa,f3fa
  //   ,f5fe,237*f3fa,f1fc,b1fc,10*f3fa,f3ff,d7fe,e7fe,253*f3fa,f7de
  //   ,b1fc,d7fe,253*f3fa,e3ba,f3fa,b1fc,253*f3fa,f7de,255*f3fa,d1ba
  //   ,7*f3fa,256*f7da,8*f1bb,8*f1fb,e1bb,d1bb,6*f3fb,e1fb,e1fb,6*f3fb
  //   ,8*f47f,8*b5ff,8*f5ff,8*f87f,8*b9ff,16*f9ff,8*f3ff,8*f1fb,8*f1bb
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  //   contents of _2ROM (hex, n*v repeats v):
  //   256*d428,8*d42a,8*d42e,8*d428,d42c,d42c,6*d428,16*d42a,8*d40a
  //   ,16*d42c,8*d40c,8*d42c,8*d428,8*55ee,8*55ea,8*5dee,8*5d6e,8*556e
  //   ,8*576e,8*576a,8*56ee,8*566e,8*5dea,8*556a,16*c42a,8*5d2c,8*5d28
  //   ,15*d428,d408,d420,d430,d428,d429,d428,d428,d408,d428,d428,d428
  //   ,d408,d428,d428,d428,d42a,d42a,5*d428,9428,90*d428,8*d42a,154*d428
  //   ,5428,d428,d428,d428,5428,237*d428,d408,11*d428,9428,1287*d428
  //   ,8*d42a,8*d42e,8*d428,d42c,d42c,6*d428,16*d42a,8*d40a,16*d42c
  //   ,8*d40c,8*d42c,8*d428,8*55ee,8*55ea,8*5dee,8*5d6e,8*556e,8*576e
  //   ,8*576a,8*56ee,8*566e,8*5dea,8*556a,16*c42a,8*5d2c,8*5d28,15*d428
  //   ,d408,d420,d430,d428,d429,d428,d428,d408,d428,d428,d428,d408,d428,d428,d428
  //   ,d42a,d42a,5*d428,9428,90*d428,8*d42a,154*d428,5428,d428,d428,d428
  //   ,5428,237*d428,d408,11*d428,9428,1287*d428,8*d42a,8*d42e,8*d428
  //   ,d42c,d42c,6*d428,16*d42a,8*d40a,16*d42c,8*d40c,8*d42c,8*d428
  //   ,8*55ee,8*55ea,8*5dee,8*5d6e,8*556e,8*576e,8*576a,8*56ee,8*566e
  //   ,8*5dea,8*556a,16*c42a,8*5d2c,8*5d28,15*d428,d408,d420,d430,d428
  //   ,d429,d428,d428,d408,d428,d428,d428,d408,d428,d428,d428,d42a,d42a
  //   ,5*d428,9428,90*d428,8*d42a,154*d428,5428,d428,d428,d428,5428
  //   ,237*d428,d408,11*d428,9428,1287*d428,8*d42a,8*d42e,8*d428,d42c,d42c
  //   ,6*d428,16*d42a,8*d40a,16*d42c,8*d40c,8*d42c,8*d428,8*55ee,8*55ea
  //   ,8*5dee,8*5d6e,8*556e,8*576e,8*576a,8*56ee,8*566e,8*5dea,8*556a
  //   ,16*c42a,8*5d2c,8*5d28,15*d428,d408,d420,d430,d428,d429,d428,d428
  //   ,d408,d428,d428,d428,d408,d428,d428,d428,d42a,d42a,5*d428,9428
  //   ,90*d428,8*d42a,154*d428,5428,d428,d428,d428,5428,237*d428,d408
  //   ,11*d428,9428,1287*d428,8*d42a,8*d42e,8*d428,d42c,d42c,6*d428
  //   ,16*d42a,8*d40a,16*d42c,8*d40c,8*d42c,8*d428,8*55ee,8*55ea,8*5dee
  //   ,8*5d6e,8*556e,8*576e,8*576a,8*56ee,8*566e,8*5dea,8*556a,16*c42a
  //   ,8*5d2c,8*5d28,15*d428,d408,d420,d430,d428,d429,d428,d428,d408
  //   ,d428,d428,d428,d408,d428,d428,d428,d42a,d42a,5*d428,9428,90*d428
  //   ,8*d42a,154*d428,5428,d428,d428,d428,5428,237*d428,d408,11*d428
  //   ,9428,1287*d428,8*d42a,8*d42e,8*d428,d42c,d42c,6*d428,16*d42a
  //   ,8*d40a,16*d42c,8*d40c,8*d42c,8*d428,8*55ee,8*55ea,8*5dee,8*5d6e
  //   ,8*556e,8*576e,8*576a,8*56ee,8*566e,8*5dea,8*556a,16*c42a,8*5d2c
  //   ,8*5d28,15*d428,d408,d420,d430,d428,d429,d428,d428,d408,d428,d428,d428
  //   ,d408,d428,d428,d428,d42a,d42a,5*d428,9428,90*d428,8*d42a,154*d428
  //   ,5428,d428,d428,d428,5428,237*d428,d408,11*d428,9428,1287*d428
  //   ,8*d42a,8*d42e,8*d428,d42c,d42c,6*d428,16*d42a,8*d40a,16*d42c
  //   ,8*d40c,8*d42c,8*d428,8*55ee,8*55ea,8*5dee,8*5d6e,8*556e,8*576e
  //   ,8*576a,8*56ee,8*566e,8*5dea,8*556a,16*c42a,8*5d2c,8*5d28,15*d428
  //   ,d408,d420,d430,d428,d429,d428,d428,d408,d428,d428,d428,d408,d428,d428,d428
  //   ,d42a,d42a,5*d428,9428,90*d428,8*d42a,154*d428,5428,d428,d428,d428
  //   ,5428,237*d428,d408,11*d428,9428,1287*d428,8*d42a,8*d42e,8*d428
  //   ,d42c,d42c,6*d428,16*d42a,8*d40a,16*d42c,8*d40c,8*d42c,8*d428
  //   ,8*55ee,8*55ea,8*5dee,8*5d6e,8*556e,8*576e,8*576a,8*56ee,8*566e
  //   ,8*5dea,8*556a,16*c42a,8*5d2c,8*5d28,15*d428,d408,d420,d430,d428
  //   ,d429,d428,d428,d408,d428,d428,d428,d408,d428,d428,d428,d42a,d42a
  //   ,5*d428,9428,90*d428,8*d42a,154*d428,5428,d428,d428,d428,5428
  //   ,237*d428,d408,11*d428,9428,1287*d428,8*d42a,8*d42e,8*d428,d42c,d42c
  //   ,6*d428,16*d42a,8*d40a,16*d42c,8*d40c,8*d42c,8*d428,8*55ee,8*55ea
  //   ,8*5dee,8*5d6e,8*556e,8*576e,8*576a,8*56ee,8*566e,8*5dea,8*556a
  //   ,16*c42a,8*5d2c,8*5d28,15*d428,d408,d420,d430,d428,d429,d428,d428
  //   ,d408,d428,d428,d428,d408,d428,d428,d428,d42a,d42a,5*d428,9428
  //   ,90*d428,8*d42a,154*d428,5428,d428,d428,d428,5428,237*d428,d408
  //   ,11*d428,9428,1287*d428,8*d42a,8*d42e,8*d428,d42c,d42c,6*d428
  //   ,16*d42a,8*d40a,16*d42c,8*d40c,8*d42c,8*d428,8*55ee,8*55ea,8*5dee
  //   ,8*5d6e,8*556e,8*576e,8*576a,8*56ee,8*566e,8*5dea,8*556a,16*c42a
  //   ,8*5d2c,8*5d28,15*d428,d408,d420,d430,d428,d429,d428,d428,d408
  //   ,d428,d428,d428,d408,d428,d428,d428,d42a,d42a,5*d428,9428,90*d428
  //   ,8*d42a,154*d428,5428,d428,d428,d428,5428,237*d428,d408,11*d428
  //   ,9428,1287*d428,8*d42a,8*d42e,8*d428,d42c,d42c,6*d428,16*d42a
  //   ,8*d40a,16*d42c,8*d40c,8*d42c,8*d428,8*55ee,8*55ea,8*5dee,8*5d6e
  //   ,8*556e,8*576e,8*576a,8*56ee,8*566e,8*5dea,8*556a,16*c42a,8*5d2c
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  //   contents of _3ROM (hex, n*v repeats v):
  //   336*fd0,8*f60,8*f40,140*fd0,f60,f60,fd0,fd0,f90,ed0,f90,fc0,fe0
  //   ,fd0,dd0,ed0,f60,f40,f40,fdc,fd8,f60,f40,89*fd0,8*f50,140*fd0
  //   ,f60,f60,fd0,fd0,fd0,dd0,6*fd0,f60,f40,f49,fd0,fd0,fd0,f50,249*fd0
  //   ,f60,f50,f40,253*fd0,7d0,fd0,f50,509*fd0,17d0,599*fd0,8*f60,8*f40
  //   ,140*fd0,f60,f60,fd0,fd0,f90,ed0,f90,fc0,fe0,fd0,dd0,ed0,f60,f40,f40
  //   ,fdc,fd8,f60,f40,89*fd0,8*f50,140*fd0,f60,f60,fd0,fd0,fd0,dd0
  //   ,6*fd0,f60,f40,f49,fd0,fd0,fd0,f50,249*fd0,f60,f50,f40,253*fd0
  //   ,7d0,fd0,f50,509*fd0,17d0,599*fd0,8*f60,8*f40,140*fd0,f60,f60
  //   ,fd0,fd0,f90,ed0,f90,fc0,fe0,fd0,dd0,ed0,f60,f40,f40,fdc,fd8,f60
  //   ,f40,89*fd0,8*f50,140*fd0,f60,f60,fd0,fd0,fd0,dd0,6*fd0,f60,f40
  //   ,f49,fd0,fd0,fd0,f50,249*fd0,f60,f50,f40,253*fd0,7d0,fd0,f50,509*fd0
  //   ,17d0,599*fd0,8*f60,8*f40,140*fd0,f60,f60,fd0,fd0,f90,ed0,f90
  //   ,fc0,fe0,fd0,dd0,ed0,f60,f40,f40,fdc,fd8,f60,f40,89*fd0,8*f50
  //   ,140*fd0,f60,f60,fd0,fd0,fd0,dd0,6*fd0,f60,f40,f49,fd0,fd0,fd0
  //   ,f50,249*fd0,f60,f50,f40,253*fd0,7d0,fd0,f50,509*fd0,17d0,599*fd0
  //   ,8*f60,8*f40,140*fd0,f60,f60,fd0,fd0,f90,ed0,f90,fc0,fe0,fd0,dd0
  //   ,ed0,f60,f40,f40,fdc,fd8,f60,f40,89*fd0,8*f50,140*fd0,f60,f60
  //   ,fd0,fd0,fd0,dd0,6*fd0,f60,f40,f49,fd0,fd0,fd0,f50,249*fd0,f60
  //   ,f50,f40,253*fd0,7d0,fd0,f50,509*fd0,17d0,599*fd0,8*f60,8*f40
  //   ,140*fd0,f60,f60,fd0,fd0,f90,ed0,f90,fc0,fe0,fd0,dd0,ed0,f60,f40,f40
  //   ,fdc,fd8,f60,f40,89*fd0,8*f50,140*fd0,f60,f60,fd0,fd0,fd0,dd0
  //   ,6*fd0,f60,f40,f49,fd0,fd0,fd0,f50,249*fd0,f60,f50,f40,253*fd0
  //   ,7d0,fd0,f50,509*fd0,17d0,599*fd0,8*f60,8*f40,140*fd0,f60,f60
  //   ,fd0,fd0,f90,ed0,f90,fc0,fe0,fd0,dd0,ed0,f60,f40,f40,fdc,fd8,f60
  //   ,f40,89*fd0,8*f50,140*fd0,f60,f60,fd0,fd0,fd0,dd0,6*fd0,f60,f40
  //   ,f49,fd0,fd0,fd0,f50,249*fd0,f60,f50,f40,253*fd0,7d0,fd0,f50,509*fd0
  //   ,17d0,599*fd0,8*f60,8*f40,140*fd0,f60,f60,fd0,fd0,f90,ed0,f90
  //   ,fc0,fe0,fd0,dd0,ed0,f60,f40,f40,fdc,fd8,f60,f40,89*fd0,8*f50
  //   ,140*fd0,f60,f60,fd0,fd0,fd0,dd0,6*fd0,f60,f40,f49,fd0,fd0,fd0
  //   ,f50,249*fd0,f60,f50,f40,253*fd0,7d0,fd0,f50,509*fd0,17d0,599*fd0
  //   ,8*f60,8*f40,140*fd0,f60,f60,fd0,fd0,f90,ed0,f90,fc0,fe0,fd0,dd0
  //   ,ed0,f60,f40,f40,fdc,fd8,f60,f40,89*fd0,8*f50,140*fd0,f60,f60
  //   ,fd0,fd0,fd0,dd0,6*fd0,f60,f40,f49,fd0,fd0,fd0,f50,249*fd0,f60
  //   ,f50,f40,253*fd0,7d0,fd0,f50,509*fd0,17d0,599*fd0,8*f60,8*f40
  //   ,140*fd0,f60,f60,fd0,fd0,f90,ed0,f90,fc0,fe0,fd0,dd0,ed0,f60,f40,f40
  //   ,fdc,fd8,f60,f40,89*fd0,8*f50,140*fd0,f60,f60,fd0,fd0,fd0,dd0
  //   ,6*fd0,f60,f40,f49,fd0,fd0,fd0,f50,249*fd0,f60,f50,f40,253*fd0
  //   ,7d0,fd0,f50,509*fd0,17d0,599*fd0,8*f60,8*f40,140*fd0,f60,f60
  //   ,fd0,fd0,f90,ed0,f90,fc0,fe0,fd0,dd0,ed0,f60,f40,f40,fdc,fd8,f60
  //   ,f40,89*fd0,8*f50,140*fd0,f60,f60,fd0,fd0,fd0,dd0,6*fd0,f60,f40
  //   ,f49,fd0,fd0,fd0,f50,249*fd0,f60,f50,f40,253*fd0,7d0,fd0,f50,509*fd0
  //   ,17d0,599*fd0,8*f60,8*f40,140*fd0,f60,f60,fd0,fd0,f90,ed0,f90
  //   ,fc0,fe0,fd0,dd0,ed0,f60,f40,f40,fdc,fd8,f60,f40,89*fd0,8*f50
  //   ,140*fd0,f60,f60,fd0,fd0,fd0,dd0,6*fd0,f60,f40,f49,fd0,fd0,fd0
  //   ,f50,249*fd0,f60,f50,f40,253*fd0,7d0,fd0,f50,509*fd0,17d0,599*fd0
  //   ,8*f60,8*f40,140*fd0,f60,f60,fd0,fd0,f90,ed0,f90,fc0,fe0,fd0,dd0
  //   ,ed0,f60,f40,f40,fdc,fd8,f60,f40,89*fd0,8*f50,140*fd0,f60,f60
  //   ,fd0,fd0,fd0,dd0,6*fd0,f60,f40,f49,fd0,fd0,fd0,f50,249*fd0,f60
  //   ,f50,f40,253*fd0,7d0,fd0,f50,509*fd0,17d0,599*fd0,8*f60,8*f40
  //   ,140*fd0,f60,f60,fd0,fd0,f90,ed0,f90,fc0,fe0,fd0,dd0,ed0,f60,f40,f40
  //   ,fdc,fd8,f60,f40,89*fd0,8*f50,140*fd0,f60,f60,fd0,fd0,fd0,dd0
  //   ,6*fd0,f60,f40,f49,fd0,fd0,fd0,f50,249*fd0,f60,f50,f40,253*fd0
  //   ,7d0,fd0,f50,509*fd0,17d0,599*fd0,8*f60,8*f40,140*fd0,f60,f60
  //   ,fd0,fd0,f90,ed0,f90,fc0,fe0,fd0,dd0,ed0,f60,f40,f40,fdc,fd8,f60
  //   ,f40,89*fd0,8*f50,140*fd0,f60,f60,fd0,fd0,fd0,dd0,6*fd0,f60,f40
  //   ,f49,fd0,fd0,fd0,f50,249*fd0,f60,f50,f40,253*fd0,7d0,fd0,f50,509*fd0
  //   ,17d0,599*fd0,8*f60,8*f40,140*fd0,f60,f60,fd0,fd0,f90,ed0,f90
  //   ,fc0,fe0,fd0,dd0,ed0,f60,f40,f40,fdc,fd8,f60,f40,89*fd0,8*f50
  //   ,140*fd0,f60,f60,fd0,fd0,fd0,dd0,6*fd0,f60,f40,f49,fd0,fd0,fd0
  //   ,f50,249*fd0,f60,f50,f40,253*fd0,7d0,fd0,f50,509*fd0,17d0,263*fd0
  //   ,768*f60,256*7d0,256*fd0,256*17d0,256*fd0,256*bdc,768*f60,256*7d0
  //   ,256*fd0,256*17d0,256*fd0,256*bdc,768*f60,256*7d0,256*fd0,256*17d0
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endmodule
