// Digital circuit FLAG_REG.dig as structural Verilog
module FLAG_REG (
  input  [7:0] D_IN,
  input  Z_FLAG,
  input  C_FLAG,
  input  N_FLAG,
  input  V_FLAG,
  input  I_SET,
  input  I_WRITE,
  input  nFL_OE,
  input  nFL_LD,
  input  FL_SEL,
  input  FB,
  input  CLK,
  input  nRST,
  output [7:0] D_OUT,
  output Z,
  output C,
  output N,
  output V,
  output I
);

  wire _7432_1_pin3, _74157_1_pin4, _74157_2_pin4, _74157_2_pin7, _74157_2_pin9, _74157_2_pin12, and_1_out;

  and and_1 (and_1_out, I_WRITE, CLK);
  _74157 _74157_1 (
    .pin1(FL_SEL), .pin2(I_SET), .pin3(D_IN[4]), .pin4(_74157_1_pin4), .pin5(1'b0), .pin6(1'b0), .pin8(1'b0),
    .pin10(1'b0), .pin11(1'b0), .pin13(1'b0), .pin14(1'b0), .pin15(1'b0), .pin16(1'b1));  // open: pin7, pin9, pin12
  _74157 _74157_2 (
    .pin1(FL_SEL), .pin2(Z_FLAG), .pin3(D_IN[0]), .pin4(_74157_2_pin4), .pin5(C_FLAG), .pin6(D_IN[1]),
    .pin7(_74157_2_pin7), .pin8(1'b0), .pin9(_74157_2_pin9), .pin10(D_IN[2]), .pin11(N_FLAG),
    .pin12(_74157_2_pin12), .pin13(D_IN[3]), .pin14(V_FLAG), .pin15(1'b0), .pin16(1'b1));
  _7474 _7474_1 (
    .pin1(nRST), .pin2(_74157_1_pin4), .pin3(and_1_out), .pin4(1'b1), .pin5(I), .pin7(1'b0), .pin10(1'b0),
    .pin11(1'b0), .pin12(1'b0), .pin13(1'b0), .pin14(1'b1));  // open: pin6, pin8, pin9
  _74173 _74173_1 (
    .pin1(1'b0), .pin2(1'b0), .pin3(Z), .pin4(C), .pin5(N), .pin6(V), .pin7(CLK), .pin8(1'b0), .pin9(nFL_LD),
    .pin10(nFL_LD), .pin11(_74157_2_pin12), .pin12(_74157_2_pin9), .pin13(_74157_2_pin7),
    .pin14(_74157_2_pin4), .pin15(1'b0), .pin16(1'b1));
  _7432 _7432_1 (
    .pin1(1'b0), .pin2(FB), .pin3(_7432_1_pin3), .pin4(1'b0), .pin5(1'b0), .pin7(1'b0), .pin9(1'b0),
    .pin10(1'b0), .pin12(1'b0), .pin13(1'b0), .pin14(1'b1));  // open: pin6, pin8, pin11
  _74245 _74245_1 (
    .pin1(1'b0), .pin2(D_OUT[0]), .pin3(D_OUT[1]), .pin4(D_OUT[2]), .pin5(D_OUT[3]), .pin6(D_OUT[4]),
    .pin7(D_OUT[5]), .pin8(D_OUT[6]), .pin9(D_OUT[7]), .pin10(1'b0), .pin11(1'b0), .pin12(1'b0),
    .pin13(_7432_1_pin3), .pin14(I), .pin15(V), .pin16(N), .pin17(C), .pin18(Z), .pin19(nFL_OE), .pin20(1'b1));
endmodule
