// Digital circuit IR.dig as structural Verilog
module IR (
  input  [15:0] ROM_IN,
  input  nIR_LD,
  input  nIRD_OE,
  input  nIRA_OE,
  input  CLK,
  output [4:0] _15_11,
  output [2:0] _10_8,
  output _8,
  output [2:0] _7_5,
  output [7:0] _0_7,
  output [7:0] AB
);

  wire I0, I1, I2, I3, I4;

  _74377 _74377_1 (
    .pin1(nIR_LD), .pin2(_8), .pin3(ROM_IN[8]), .pin4(ROM_IN[9]), .pin5(_10_8[1]), .pin6(_10_8[2]),
    .pin7(ROM_IN[10]), .pin8(ROM_IN[11]), .pin9(_15_11[0]), .pin10(1'b0), .pin11(CLK), .pin12(_15_11[1]),
    .pin13(ROM_IN[12]), .pin14(ROM_IN[13]), .pin15(_15_11[2]), .pin16(_15_11[3]), .pin17(ROM_IN[14]),
    .pin18(ROM_IN[15]), .pin19(_15_11[4]), .pin20(1'b1));
  _74377 _74377_2 (
    .pin1(nIR_LD), .pin2(I0), .pin3(ROM_IN[0]), .pin4(ROM_IN[1]), .pin5(I1), .pin6(I2), .pin7(ROM_IN[2]),
    .pin8(ROM_IN[3]), .pin9(I3), .pin10(1'b0), .pin11(CLK), .pin12(I4), .pin13(ROM_IN[4]), .pin14(ROM_IN[5]),
    .pin15(_7_5[0]), .pin16(_7_5[1]), .pin17(ROM_IN[6]), .pin18(ROM_IN[7]), .pin19(_7_5[2]), .pin20(1'b1));
  _74245 _74245_1 (
    .pin1(1'b0), .pin2(_0_7[0]), .pin3(_0_7[1]), .pin4(_0_7[2]), .pin5(_0_7[3]), .pin6(_0_7[4]),
    .pin7(_0_7[5]), .pin8(_0_7[6]), .pin9(_0_7[7]), .pin10(1'b0), .pin11(_7_5[2]), .pin12(_7_5[1]),
    .pin13(_7_5[0]), .pin14(I4), .pin15(I3), .pin16(I2), .pin17(I1), .pin18(I0), .pin19(nIRD_OE), .pin20(1'b1));
  _74245 _74245_2 (
    .pin1(1'b1), .pin2(I0), .pin3(I1), .pin4(I2), .pin5(I3), .pin6(I4), .pin7(_7_5[0]), .pin8(_7_5[1]),
    .pin9(_7_5[2]), .pin10(1'b0), .pin11(AB[7]), .pin12(AB[6]), .pin13(AB[5]), .pin14(AB[4]), .pin15(AB[3]),
    .pin16(AB[2]), .pin17(AB[1]), .pin18(AB[0]), .pin19(nIRA_OE), .pin20(1'b1));

  assign _10_8[0] = _8;

  // Other names for the same wires on the sheet: A0 = AB[0]; A1 = AB[1]; A2 = AB[2]; A3 = AB[3]; A4 = AB[4];
  //   A5 = AB[5]; A6 = AB[6]; A7 = AB[7]; D0 = _0_7[0]; D1 = _0_7[1]; D2 = _0_7[2]; D3 = _0_7[3]; D4 = _0_7[4];
  //   D5 = _0_7[5]; D6 = _0_7[6]; D7 = _0_7[7]; I5 = _7_5[0]; I6 = _7_5[1]; I7 = _7_5[2]; I8 = _8; I9 = _10_8[1];
  //   I10 = _10_8[2]; I11 = _15_11[0]; I12 = _15_11[1]; I13 = _15_11[2]; I14 = _15_11[3]; I15 = _15_11[4];
  //   IR_LD = nIR_LD; R0 = ROM_IN[0]; R1 = ROM_IN[1]; R2 = ROM_IN[2]; R3 = ROM_IN[3]; R4 = ROM_IN[4]; R5 = ROM_IN[5];
  //   R6 = ROM_IN[6]; R7 = ROM_IN[7]; R8 = ROM_IN[8]; R9 = ROM_IN[9]; R10 = ROM_IN[10]; R11 = ROM_IN[11];
  //   R12 = ROM_IN[12]; R13 = ROM_IN[13]; R14 = ROM_IN[14]; R15 = ROM_IN[15]
endmodule
