// Digital circuit IRQ_LATCH.dig as structural Verilog
module IRQ_LATCH (
  input  IRQ,
  input  I,
  input  nCLR_IRQ,
  output IRQ_PEND
);

  wire _7474_1_pin5;

  _7474 _7474_1 (
    .pin1(nCLR_IRQ), .pin2(1'b1), .pin3(IRQ), .pin4(1'b1), .pin5(_7474_1_pin5), .pin7(1'b0), .pin10(1'b0),
    .pin11(1'b0), .pin12(1'b0), .pin13(1'b0), .pin14(1'b1));  // open: pin6, pin8, pin9
  _7408 _7408_1 (
    .pin1(_7474_1_pin5), .pin2(I), .pin3(IRQ_PEND), .pin4(1'b0), .pin5(1'b0), .pin7(1'b0), .pin9(1'b0),
    .pin10(1'b0), .pin12(1'b0), .pin13(1'b0), .pin14(1'b1));  // open: pin6, pin8, pin11
endmodule
