// Digital circuit MAR.dig as structural Verilog
module MAR (
  input  [7:0] D_IN,
  input  nMARL_LD,
  input  nMARH_LD,
  input  nMAR_OE,
  input  nMAR_INC,
  input  MAR_DIR,
  input  CLK,
  output [15:0] A_OUT
);

  wire _74191_1_pin2, _74191_1_pin3, _74191_1_pin4, _74191_1_pin6, _74191_1_pin7, _74191_2_pin2,
       _74191_2_pin3, _74191_2_pin4, _74191_2_pin6, _74191_2_pin7, _74191_3_pin2, _74191_3_pin3,
       _74191_3_pin4, _74191_3_pin6, _74191_3_pin7, _74191_4_pin2, _74191_4_pin3, _74191_4_pin6,
       _74191_4_pin7, nMARH_LD_t, nMARL_LD_t;

  or or_1 (nMARL_LD_t, nMARL_LD, CLK);
  or or_2 (nMARH_LD_t, nMARH_LD, CLK);
  _74191 _74191_1 (
    .pin1(D_IN[5]), .pin2(_74191_1_pin2), .pin3(_74191_1_pin3), .pin4(_74191_1_pin4), .pin5(MAR_DIR),
    .pin6(_74191_1_pin6), .pin7(_74191_1_pin7), .pin8(1'b0), .pin9(D_IN[7]), .pin10(D_IN[6]),
    .pin11(nMARH_LD_t), .pin14(CLK), .pin15(D_IN[4]), .pin16(1'b1));  // open: pin12, pin13
  _74191 _74191_2 (
    .pin1(D_IN[1]), .pin2(_74191_2_pin2), .pin3(_74191_2_pin3), .pin4(_74191_2_pin4), .pin5(MAR_DIR),
    .pin6(_74191_2_pin6), .pin7(_74191_2_pin7), .pin8(1'b0), .pin9(D_IN[3]), .pin10(D_IN[2]),
    .pin11(nMARH_LD_t), .pin13(_74191_1_pin4), .pin14(CLK), .pin15(D_IN[0]), .pin16(1'b1));  // open: pin12
  _74191 _74191_3 (
    .pin1(D_IN[5]), .pin2(_74191_3_pin2), .pin3(_74191_3_pin3), .pin4(_74191_3_pin4), .pin5(MAR_DIR),
    .pin6(_74191_3_pin6), .pin7(_74191_3_pin7), .pin8(1'b0), .pin9(D_IN[7]), .pin10(D_IN[6]),
    .pin11(nMARL_LD_t), .pin13(_74191_2_pin4), .pin14(CLK), .pin15(D_IN[4]), .pin16(1'b1));  // open: pin12
  _74191 _74191_4 (
    .pin1(D_IN[1]), .pin2(_74191_4_pin2), .pin3(_74191_4_pin3), .pin4(nMAR_INC), .pin5(MAR_DIR),
    .pin6(_74191_4_pin6), .pin7(_74191_4_pin7), .pin8(1'b0), .pin9(D_IN[3]), .pin10(D_IN[2]),
    .pin11(nMARL_LD_t), .pin13(_74191_3_pin4), .pin14(CLK), .pin15(D_IN[0]), .pin16(1'b1));  // open: pin12
  _74245 _74245_1 (
    .pin1(1'b0), .pin2(A_OUT[8]), .pin3(A_OUT[9]), .pin4(A_OUT[10]), .pin5(A_OUT[11]), .pin6(A_OUT[12]),
    .pin7(A_OUT[13]), .pin8(A_OUT[14]), .pin9(A_OUT[15]), .pin10(1'b0), .pin11(_74191_1_pin7),
    .pin12(_74191_1_pin6), .pin13(_74191_1_pin2), .pin14(_74191_1_pin3), .pin15(_74191_2_pin7),
    .pin16(_74191_2_pin6), .pin17(_74191_2_pin2), .pin18(_74191_2_pin3), .pin19(nMAR_OE), .pin20(1'b1));
  _74245 _74245_2 (
    .pin1(1'b0), .pin2(A_OUT[0]), .pin3(A_OUT[1]), .pin4(A_OUT[2]), .pin5(A_OUT[3]), .pin6(A_OUT[4]),
    .pin7(A_OUT[5]), .pin8(A_OUT[6]), .pin9(A_OUT[7]), .pin10(1'b0), .pin11(_74191_3_pin7),
    .pin12(_74191_3_pin6), .pin13(_74191_3_pin2), .pin14(_74191_3_pin3), .pin15(_74191_4_pin7),
    .pin16(_74191_4_pin6), .pin17(_74191_4_pin2), .pin18(_74191_4_pin3), .pin19(nMAR_OE), .pin20(1'b1));
endmodule
