// Digital circuit MMIO.dig as structural Verilog
module MMIO (
  input  [15:0] A_IN,
  input  [7:0] D_IN,
  input  nMMIO_CS,
  input  MEM_WR,
  input  MEM_RD,
  input  [7:0] KB_IN,
  input  KB_ST,
  output [7:0] D_OUT,
  output [3:0] SPI_OUT,
  output [7:0] DISPLAY,
  output KB_EN
);

  wire _7400_1_pin13, _7404_1_pin2, _7404_1_pin10, _7404_1_pin12, _74138_1_pin7, _74138_1_pin14,
       _74138_1_pin15, DSP_SEL, KBST_RD, MEM_WR_t, SPI_SEL;

  _74138 _74138_1 (
    .pin1(A_IN[0]), .pin2(A_IN[1]), .pin3(A_IN[2]), .pin4(nMMIO_CS), .pin5(1'b0), .pin6(1'b1),
    .pin7(_74138_1_pin7), .pin8(1'b0), .pin12(DSP_SEL), .pin13(SPI_SEL), .pin14(_74138_1_pin14),
    .pin15(_74138_1_pin15), .pin16(1'b1));  // open: pin9, pin10, pin11
  _7404 _7404_1 (
    .pin1(nMMIO_CS), .pin2(_7404_1_pin2), .pin3(1'b0), .pin5(1'b0), .pin7(1'b0), .pin9(1'b0),
    .pin10(_7404_1_pin10), .pin11(_74138_1_pin14), .pin12(_7404_1_pin12), .pin13(_74138_1_pin15), .pin14(1'b1));  // open: pin4, pin6, pin8
  _7400 _7400_1 (
    .pin1(_7404_1_pin2), .pin2(MEM_WR), .pin3(MEM_WR_t), .pin4(1'b0), .pin5(1'b0), .pin7(1'b0),
    .pin8(KBST_RD), .pin9(MEM_RD), .pin10(_7404_1_pin10), .pin11(KB_EN), .pin12(MEM_RD),
    .pin13(_7400_1_pin13), .pin14(1'b1));  // open: pin6
  and and_1 (_7400_1_pin13, _7404_1_pin12, _7404_1_pin2);
  _74377 _74377_1 (
    .pin1(SPI_SEL), .pin2(SPI_OUT[0]), .pin3(D_IN[0]), .pin4(D_IN[1]), .pin5(SPI_OUT[1]), .pin6(SPI_OUT[2]),
    .pin7(D_IN[2]), .pin8(D_IN[3]), .pin9(SPI_OUT[3]), .pin10(1'b0), .pin11(MEM_WR_t), .pin13(1'b0),
    .pin14(1'b0), .pin17(1'b0), .pin18(1'b0), .pin20(1'b1));  // open: pin12, pin15, pin16, pin19
  _74377 _74377_2 (
    .pin1(DSP_SEL), .pin2(DISPLAY[0]), .pin3(D_IN[0]), .pin4(D_IN[1]), .pin5(DISPLAY[1]), .pin6(DISPLAY[2]),
    .pin7(D_IN[2]), .pin8(D_IN[3]), .pin9(DISPLAY[3]), .pin10(1'b0), .pin11(MEM_WR_t), .pin12(DISPLAY[4]),
    .pin13(D_IN[4]), .pin14(D_IN[5]), .pin15(DISPLAY[5]), .pin16(DISPLAY[6]), .pin17(D_IN[6]),
    .pin18(D_IN[7]), .pin19(DISPLAY[7]), .pin20(1'b1));
  _74245 _74245_1 (
    .pin1(1'b1), .pin2(KB_IN[0]), .pin3(KB_IN[1]), .pin4(KB_IN[2]), .pin5(KB_IN[3]), .pin6(KB_IN[4]),
    .pin7(KB_IN[5]), .pin8(KB_IN[6]), .pin9(KB_IN[7]), .pin10(1'b0), .pin11(D_OUT[7]), .pin12(D_OUT[6]),
    .pin13(D_OUT[5]), .pin14(D_OUT[4]), .pin15(D_OUT[3]), .pin16(D_OUT[2]), .pin17(D_OUT[1]),
    .pin18(D_OUT[0]), .pin19(KB_EN), .pin20(1'b1));
  _74245 _74245_2 (
    .pin1(1'b1), .pin2(1'b0), .pin3(1'b0), .pin4(1'b0), .pin5(1'b0), .pin6(1'b0), .pin7(1'b0), .pin8(1'b0),
    .pin9(KB_ST), .pin10(1'b0), .pin11(D_OUT[7]), .pin12(D_OUT[6]), .pin13(D_OUT[5]), .pin14(D_OUT[4]),
    .pin15(D_OUT[3]), .pin16(D_OUT[2]), .pin17(D_OUT[1]), .pin18(D_OUT[0]), .pin19(KBST_RD), .pin20(1'b1));

  // Other names for the same wires on the sheet: KB_RD = KB_EN
endmodule
