// Digital circuit PC.dig as structural Verilog
module PC (
  input  [15:0] A_BUS_IN,
  input  PC_INC,
  input  nPC_LD,
  input  CLK,
  input  RST,
  output [15:0] AB_OUT
);

  wire nPC_LD_t, TC0, TC1, TC2;

  xor xor_1 (nPC_LD_t, RST, nPC_LD);
  _74161 _74161_1 (
    .pin1(1'b1), .pin2(CLK), .pin3(A_BUS_IN[0]), .pin4(A_BUS_IN[1]), .pin5(A_BUS_IN[2]), .pin6(A_BUS_IN[3]),
    .pin7(PC_INC), .pin8(1'b0), .pin9(nPC_LD_t), .pin10(PC_INC), .pin11(AB_OUT[3]), .pin12(AB_OUT[2]),
    .pin13(AB_OUT[1]), .pin14(AB_OUT[0]), .pin15(TC0), .pin16(1'b1));
  _74161 _74161_2 (
    .pin1(1'b1), .pin2(CLK), .pin3(A_BUS_IN[8]), .pin4(A_BUS_IN[9]), .pin5(A_BUS_IN[10]),
    .pin6(A_BUS_IN[11]), .pin7(PC_INC), .pin8(1'b0), .pin9(nPC_LD_t), .pin10(TC1), .pin11(AB_OUT[11]),
    .pin12(AB_OUT[10]), .pin13(AB_OUT[9]), .pin14(AB_OUT[8]), .pin15(TC2), .pin16(1'b1));
  _74161 _74161_3 (
    .pin1(1'b1), .pin2(CLK), .pin3(A_BUS_IN[4]), .pin4(A_BUS_IN[5]), .pin5(A_BUS_IN[6]), .pin6(A_BUS_IN[7]),
    .pin7(PC_INC), .pin8(1'b0), .pin9(nPC_LD_t), .pin10(TC0), .pin11(AB_OUT[7]), .pin12(AB_OUT[6]),
    .pin13(AB_OUT[5]), .pin14(AB_OUT[4]), .pin15(TC1), .pin16(1'b1));
  _74161 _74161_4 (
    .pin1(1'b1), .pin2(CLK), .pin3(A_BUS_IN[12]), .pin4(A_BUS_IN[13]), .pin5(A_BUS_IN[14]),
    .pin6(A_BUS_IN[15]), .pin7(PC_INC), .pin8(1'b0), .pin9(nPC_LD_t), .pin10(TC2), .pin11(AB_OUT[15]),
    .pin12(AB_OUT[14]), .pin13(AB_OUT[13]), .pin14(AB_OUT[12]), .pin16(1'b1));  // open: pin15

  // Other names for the same wires on the sheet: AI0 = A_BUS_IN[0]; AI1 = A_BUS_IN[1]; AI2 = A_BUS_IN[2];
  //   AI3 = A_BUS_IN[3]; AI4 = A_BUS_IN[4]; AI5 = A_BUS_IN[5]; AI6 = A_BUS_IN[6]; AI7 = A_BUS_IN[7];
  //   AI8 = A_BUS_IN[8]; AI9 = A_BUS_IN[9]; AI10 = A_BUS_IN[10]; AI11 = A_BUS_IN[11]; AI12 = A_BUS_IN[12];
  //   AI13 = A_BUS_IN[13]; AI14 = A_BUS_IN[14]; AI15 = A_BUS_IN[15]; AO0 = AB_OUT[0]; AO1 = AB_OUT[1];
  //   AO2 = AB_OUT[2]; AO3 = AB_OUT[3]; AO4 = AB_OUT[4]; AO5 = AB_OUT[5]; AO6 = AB_OUT[6]; AO7 = AB_OUT[7];
  //   AO8 = AB_OUT[8]; AO9 = AB_OUT[9]; AO10 = AB_OUT[10]; AO11 = AB_OUT[11]; AO12 = AB_OUT[12]; AO13 = AB_OUT[13];
  //   AO14 = AB_OUT[14]; AO15 = AB_OUT[15]
endmodule
