// Digital circuit RST Buffer.dig as structural Verilog
module RST_Buffer (
  input  RST,
  output [7:0] A_BUS__0_7
);

  _74245 _74245_1 (
    .pin1(1'b1), .pin2(1'b0), .pin3(1'b0), .pin4(1'b0), .pin5(1'b0), .pin6(1'b0), .pin7(1'b0), .pin8(1'b1),
    .pin9(1'b1), .pin10(1'b0), .pin11(A_BUS__0_7[7]), .pin12(A_BUS__0_7[6]), .pin13(A_BUS__0_7[5]),
    .pin14(A_BUS__0_7[4]), .pin15(A_BUS__0_7[3]), .pin16(A_BUS__0_7[2]), .pin17(A_BUS__0_7[1]),
    .pin18(A_BUS__0_7[0]), .pin19(RST), .pin20(1'b1));
  // Pins of 1 and 8 bits meet at A_BUS__0_7
endmodule
