// Digital circuit RST_HARDWARE.dig as structural Verilog
module RST_HARDWARE (
  input  CLK,
  input  RST_IN,
  output RST
);

  wire _7474_1_pin1, RST_IN_t;

  not not_1 (RST_IN_t, RST_IN);
  _7474 _7474_1 (
    .pin1(_7474_1_pin1), .pin2(1'b0), .pin3(CLK), .pin4(RST_IN_t), .pin5(RST), .pin7(1'b0),
    .pin8(_7474_1_pin1), .pin10(1'b1), .pin11(CLK), .pin12(RST), .pin13(1'b1), .pin14(1'b1));  // open: pin6, pin9
endmodule
