// Digital circuit SP_a.dig as structural Verilog
module SP_a (
  input  [15:0] A_IN,
  input  nSP_INC,
  input  SP_DIR,
  input  nSP_LD,
  input  nSP_OE,
  input  nSPH_OE,
  input  nSPL_OE,
  input  CLK,
  output [15:0] A_OUT,
  output [7:0] D_OUT
);

  wire _74191_1_pin2, _74191_1_pin3, _74191_1_pin4, _74191_1_pin6, _74191_1_pin7, _74191_2_pin2,
       _74191_2_pin3, _74191_2_pin4, _74191_2_pin6, _74191_2_pin7, _74191_3_pin2, _74191_3_pin3,
       _74191_3_pin4, _74191_3_pin6, _74191_3_pin7, _74191_4_pin2, _74191_4_pin3, _74191_4_pin6,
       _74191_4_pin7, nSP_LD_t;

  or or_1 (nSP_LD_t, nSP_LD, CLK);
  _74191 _74191_1 (
    .pin1(A_IN[13]), .pin2(_74191_1_pin2), .pin3(_74191_1_pin3), .pin4(_74191_1_pin4), .pin5(SP_DIR),
    .pin6(_74191_1_pin6), .pin7(_74191_1_pin7), .pin8(1'b0), .pin9(A_IN[15]), .pin10(A_IN[14]),
    .pin11(nSP_LD_t), .pin14(CLK), .pin15(A_IN[12]), .pin16(1'b1));  // open: pin12, pin13
  _74191 _74191_2 (
    .pin1(A_IN[9]), .pin2(_74191_2_pin2), .pin3(_74191_2_pin3), .pin4(_74191_2_pin4), .pin5(SP_DIR),
    .pin6(_74191_2_pin6), .pin7(_74191_2_pin7), .pin8(1'b0), .pin9(A_IN[11]), .pin10(A_IN[10]),
    .pin11(nSP_LD_t), .pin13(_74191_1_pin4), .pin14(CLK), .pin15(A_IN[8]), .pin16(1'b1));  // open: pin12
  _74191 _74191_3 (
    .pin1(A_IN[5]), .pin2(_74191_3_pin2), .pin3(_74191_3_pin3), .pin4(_74191_3_pin4), .pin5(SP_DIR),
    .pin6(_74191_3_pin6), .pin7(_74191_3_pin7), .pin8(1'b0), .pin9(A_IN[7]), .pin10(A_IN[6]),
    .pin11(nSP_LD_t), .pin13(_74191_2_pin4), .pin14(CLK), .pin15(A_IN[4]), .pin16(1'b1));  // open: pin12
  _74191 _74191_4 (
    .pin1(A_IN[1]), .pin2(_74191_4_pin2), .pin3(_74191_4_pin3), .pin4(nSP_INC), .pin5(SP_DIR),
    .pin6(_74191_4_pin6), .pin7(_74191_4_pin7), .pin8(1'b0), .pin9(A_IN[3]), .pin10(A_IN[2]),
    .pin11(nSP_LD_t), .pin13(_74191_3_pin4), .pin14(CLK), .pin15(A_IN[0]), .pin16(1'b1));  // open: pin12
  _74245 _74245_1 (
    .pin1(1'b0), .pin2(D_OUT[0]), .pin3(D_OUT[1]), .pin4(D_OUT[2]), .pin5(D_OUT[3]), .pin6(D_OUT[4]),
    .pin7(D_OUT[5]), .pin8(D_OUT[6]), .pin9(D_OUT[7]), .pin10(1'b0), .pin11(_74191_3_pin7),
    .pin12(_74191_3_pin6), .pin13(_74191_3_pin2), .pin14(_74191_3_pin3), .pin15(_74191_4_pin7),
    .pin16(_74191_4_pin6), .pin17(_74191_4_pin2), .pin18(_74191_4_pin3), .pin19(nSPL_OE), .pin20(1'b1));
  _74245 _74245_2 (
    .pin1(1'b1), .pin2(_74191_4_pin3), .pin3(_74191_4_pin2), .pin4(_74191_4_pin6), .pin5(_74191_4_pin7),
    .pin6(_74191_3_pin3), .pin7(_74191_3_pin2), .pin8(_74191_3_pin6), .pin9(_74191_3_pin7), .pin10(1'b0),
    .pin11(A_OUT[7]), .pin12(A_OUT[6]), .pin13(A_OUT[5]), .pin14(A_OUT[4]), .pin15(A_OUT[3]),
    .pin16(A_OUT[2]), .pin17(A_OUT[1]), .pin18(A_OUT[0]), .pin19(nSP_OE), .pin20(1'b1));
  _74245 _74245_3 (
    .pin1(1'b1), .pin2(_74191_2_pin3), .pin3(_74191_2_pin2), .pin4(_74191_2_pin6), .pin5(_74191_2_pin7),
    .pin6(_74191_1_pin3), .pin7(_74191_1_pin2), .pin8(_74191_1_pin6), .pin9(_74191_1_pin7), .pin10(1'b0),
    .pin11(A_OUT[15]), .pin12(A_OUT[14]), .pin13(A_OUT[13]), .pin14(A_OUT[12]), .pin15(A_OUT[11]),
    .pin16(A_OUT[10]), .pin17(A_OUT[9]), .pin18(A_OUT[8]), .pin19(nSP_OE), .pin20(1'b1));
  _74245 _74245_4 (
    .pin1(1'b0), .pin2(D_OUT[0]), .pin3(D_OUT[1]), .pin4(D_OUT[2]), .pin5(D_OUT[3]), .pin6(D_OUT[4]),
    .pin7(D_OUT[5]), .pin8(D_OUT[6]), .pin9(D_OUT[7]), .pin10(1'b0), .pin11(_74191_1_pin7),
    .pin12(_74191_1_pin6), .pin13(_74191_1_pin2), .pin14(_74191_1_pin3), .pin15(_74191_2_pin7),
    .pin16(_74191_2_pin6), .pin17(_74191_2_pin2), .pin18(_74191_2_pin3), .pin19(nSPH_OE), .pin20(1'b1));

  // Other names for the same wires on the sheet: nSP_DIR = SP_DIR
endmodule
