// Digital circuit PC_BUFFER.dig as structural Verilog
module PC_BUFFER (
  input  [15:0] PC,
  input  PC_OE,
  input  nPCH_OE,
  input  nPCL_OE,
  input  RST,
  output [15:0] A_BUS,
  output [7:0] D_BUS
);

  wire PC_OE_t;

  xor xor_1 (PC_OE_t, RST, PC_OE);
  _74245 _74245_1 (
    .pin1(1'b0), .pin2(D_BUS[0]), .pin3(D_BUS[1]), .pin4(D_BUS[2]), .pin5(D_BUS[3]), .pin6(D_BUS[4]),
    .pin7(D_BUS[5]), .pin8(D_BUS[6]), .pin9(D_BUS[7]), .pin10(1'b0), .pin11(PC[7]), .pin12(PC[6]),
    .pin13(PC[5]), .pin14(PC[4]), .pin15(PC[3]), .pin16(PC[2]), .pin17(PC[1]), .pin18(PC[0]),
    .pin19(nPCL_OE), .pin20(1'b1));
  _74245 _74245_2 (
    .pin1(1'b1), .pin2(PC[0]), .pin3(PC[1]), .pin4(PC[2]), .pin5(PC[3]), .pin6(PC[4]), .pin7(PC[5]),
    .pin8(PC[6]), .pin9(PC[7]), .pin10(1'b0), .pin11(A_BUS[7]), .pin12(A_BUS[6]), .pin13(A_BUS[5]),
    .pin14(A_BUS[4]), .pin15(A_BUS[3]), .pin16(A_BUS[2]), .pin17(A_BUS[1]), .pin18(A_BUS[0]),
    .pin19(PC_OE_t), .pin20(1'b1));
  _74245 _74245_3 (
    .pin1(1'b0), .pin2(D_BUS[0]), .pin3(D_BUS[1]), .pin4(D_BUS[2]), .pin5(D_BUS[3]), .pin6(D_BUS[4]),
    .pin7(D_BUS[5]), .pin8(D_BUS[6]), .pin9(D_BUS[7]), .pin10(1'b0), .pin11(PC[15]), .pin12(PC[14]),
    .pin13(PC[13]), .pin14(PC[12]), .pin15(PC[11]), .pin16(PC[10]), .pin17(PC[9]), .pin18(PC[8]),
    .pin19(nPCH_OE), .pin20(1'b1));
  _74245 _74245_4 (
    .pin1(1'b1), .pin2(PC[8]), .pin3(PC[9]), .pin4(PC[10]), .pin5(PC[11]), .pin6(PC[12]), .pin7(PC[13]),
    .pin8(PC[14]), .pin9(PC[15]), .pin10(1'b0), .pin11(A_BUS[15]), .pin12(A_BUS[14]), .pin13(A_BUS[13]),
    .pin14(A_BUS[12]), .pin15(A_BUS[11]), .pin16(A_BUS[10]), .pin17(A_BUS[9]), .pin18(A_BUS[8]),
    .pin19(PC_OE_t), .pin20(1'b1));
endmodule
