// Digital circuit SP_BUFFER.dig as structural Verilog
module SP_BUFFER (
  input  [7:0] SPH,
  input  [7:0] SPL,
  input  nSP_OE,
  input  nSPH_OE,
  input  nSPL_OE,
  output [15:0] A_OUT,
  output [7:0] D_BUS
);

  _74245 _74245_1 (
    .pin1(1'b1), .pin2(SPL[0]), .pin3(SPL[1]), .pin4(SPL[2]), .pin5(SPL[3]), .pin6(SPL[4]), .pin7(SPL[5]),
    .pin8(SPL[6]), .pin9(SPL[7]), .pin10(1'b0), .pin11(A_OUT[7]), .pin12(A_OUT[6]), .pin13(A_OUT[5]),
    .pin14(A_OUT[4]), .pin15(A_OUT[3]), .pin16(A_OUT[2]), .pin17(A_OUT[1]), .pin18(A_OUT[0]), .pin19(nSP_OE),
    .pin20(1'b1));
  _74245 _74245_2 (
    .pin1(1'b0), .pin2(D_BUS[0]), .pin3(D_BUS[1]), .pin4(D_BUS[2]), .pin5(D_BUS[3]), .pin6(D_BUS[4]),
    .pin7(D_BUS[5]), .pin8(D_BUS[6]), .pin9(D_BUS[7]), .pin10(1'b0), .pin11(SPL[7]), .pin12(SPL[6]),
    .pin13(SPL[5]), .pin14(SPL[4]), .pin15(SPL[3]), .pin16(SPL[2]), .pin17(SPL[1]), .pin18(SPL[0]),
    .pin19(nSPL_OE), .pin20(1'b1));
  _74245 _74245_3 (
    .pin1(1'b0), .pin2(D_BUS[0]), .pin3(D_BUS[1]), .pin4(D_BUS[2]), .pin5(D_BUS[3]), .pin6(D_BUS[4]),
    .pin7(D_BUS[5]), .pin8(D_BUS[6]), .pin9(D_BUS[7]), .pin10(1'b0), .pin11(SPH[7]), .pin12(SPH[6]),
    .pin13(SPH[5]), .pin14(SPH[4]), .pin15(SPH[3]), .pin16(SPH[2]), .pin17(SPH[1]), .pin18(SPH[0]),
    .pin19(nSPH_OE), .pin20(1'b1));
  _74245 _74245_4 (
    .pin1(1'b1), .pin2(SPH[0]), .pin3(SPH[1]), .pin4(SPH[2]), .pin5(SPH[3]), .pin6(SPH[4]), .pin7(SPH[5]),
    .pin8(SPH[6]), .pin9(SPH[7]), .pin10(1'b0), .pin11(A_OUT[15]), .pin12(A_OUT[14]), .pin13(A_OUT[13]),
    .pin14(A_OUT[12]), .pin15(A_OUT[11]), .pin16(A_OUT[10]), .pin17(A_OUT[9]), .pin18(A_OUT[8]),
    .pin19(nSP_OE), .pin20(1'b1));
endmodule
