// Digital circuit SP_discarded.dig as structural Verilog
module SP_discarded (
  input  [15:0] A_BUS,
  input  nSP_INC,
  input  SP_DIR,
  input  nSP_LD,
  input  CLK,
  output [7:0] SPH,
  output [7:0] SPL
);

  wire _74191_1_pin13, _74191_2_pin13, _74191_3_pin13, nSP_LD_t;

  or or_1 (nSP_LD_t, nSP_LD, CLK);
  _74191 _74191_1 (
    .pin1(A_BUS[1]), .pin2(SPL[1]), .pin3(SPL[0]), .pin4(nSP_INC), .pin5(SP_DIR), .pin6(SPL[2]),
    .pin7(SPL[3]), .pin8(1'b0), .pin9(A_BUS[3]), .pin10(A_BUS[2]), .pin11(nSP_LD_t), .pin13(_74191_1_pin13),
    .pin14(CLK), .pin15(A_BUS[0]), .pin16(1'b1));  // open: pin12
  _74191 _74191_2 (
    .pin1(A_BUS[5]), .pin2(SPL[5]), .pin3(SPL[4]), .pin4(_74191_1_pin13), .pin5(SP_DIR), .pin6(SPL[6]),
    .pin7(SPL[7]), .pin8(1'b0), .pin9(A_BUS[7]), .pin10(A_BUS[6]), .pin11(nSP_LD_t), .pin13(_74191_2_pin13),
    .pin14(CLK), .pin15(A_BUS[4]), .pin16(1'b1));  // open: pin12
  _74191 _74191_3 (
    .pin1(A_BUS[9]), .pin2(SPH[1]), .pin3(SPH[0]), .pin4(_74191_2_pin13), .pin5(SP_DIR), .pin6(SPH[2]),
    .pin7(SPH[3]), .pin8(1'b0), .pin9(A_BUS[11]), .pin10(A_BUS[10]), .pin11(nSP_LD_t),
    .pin13(_74191_3_pin13), .pin14(CLK), .pin15(A_BUS[8]), .pin16(1'b1));  // open: pin12
  _74191 _74191_4 (
    .pin1(A_BUS[13]), .pin2(SPH[5]), .pin3(SPH[4]), .pin4(_74191_3_pin13), .pin5(SP_DIR), .pin6(SPH[6]),
    .pin7(SPH[7]), .pin8(1'b0), .pin9(A_BUS[15]), .pin10(A_BUS[14]), .pin11(nSP_LD_t), .pin14(CLK),
    .pin15(A_BUS[12]), .pin16(1'b1));  // open: pin12, pin13

  // Other names for the same wires on the sheet: nSP_DIR = SP_DIR
endmodule
