// Digital circuit StackPointer.dig as structural Verilog
module StackPointer (
  input  [15:0] A_IN,
  input  nSP_INC,
  input  SP_DIR,
  input  nSP_LD,
  input  nSP_OE,
  input  nSPL_OE,
  input  nSPH_OE,
  input  CLK,
  output [15:0] A_OUT,
  output [7:0] D_OUT
);

  wire [15:0] counterpreset_1_out;

  CounterPreset #(.Bits(16)) counterpreset_1 (
    .en(~nSP_INC), .C(CLK), .dir(SP_DIR), .in(A_IN), .ld(~nSP_LD), .clr(1'b0), .out(counterpreset_1_out));  // open: ovf
  assign A_OUT = ~nSP_OE ? counterpreset_1_out : 16'bz;  // DriverInvSel driverinvsel_1
  assign D_OUT = ~nSPL_OE ? counterpreset_1_out[7:0] : 8'bz;  // DriverInvSel driverinvsel_2
  assign D_OUT = ~nSPH_OE ? counterpreset_1_out[15:8] : 8'bz;  // DriverInvSel driverinvsel_3
endmodule
